# Fritzing sketch Cardio_frequence_metre (saved by Fritzing 0.9.3b)
breadboards: 1

parts:
  Composant1 = Arduino Uno (Rev3)
  LED1 = LED - 5mm [color="Red (633nm)" package="5 mm [THT]"]
  R1 = Resistor [tolerance=±5% resistance=100 package=THT]
  R2 = Resistor [tolerance=±5% resistance=470k package=THT]
  C1 = Ceramic Capacitor [capacitance=100nF package="100 mil [THT, multilayer]"]
  R3 = Resistor [tolerance=±5% resistance=1k package=THT]
  R4 = Resistor [tolerance=±5% resistance=330k package=THT]
  C2 = Ceramic Capacitor [capacitance=1µF package="100 mil [THT, multilayer]"]
  R5 = Resistor [tolerance=±5% resistance=10k package=THT]
  R6 = Resistor [tolerance=±5% resistance=100 package=THT]
  IC1 = LM324 [package=dil16]
  LED2 = LED - 5mm [color="Infrared (940nm)" package="5 mm [THT]"]
  R7 = Photocell (LDR) [package=THT]

nets:
  N1: Composant1.A0, LED1.anode, R1.Pin_1
  N2: Composant1.5V, R5.Pin_0, R6.Pin_0, IC1.V+
  N3: Composant1.GND, LED1.cathode, R3.Pin_0, R4.Pin_0, LED2.cathode, R7.pin_1
  N4: R1.Pin_0, R2.Pin_1, C1.0, IC1.OUT2
  N5: R2.Pin_0, C1.1, R3.Pin_1, IC1.IN2-
  N6: R4.Pin_1, C2.0
  N7: C2.1, R5.Pin_1, IC1.IN2+, R7.pin_0
  N8: R6.Pin_1, LED2.anode
  GND: IC1.GND

custom parts:
  LM324: LM324 Quad OpAmp
